// Logisim project Processor.circ as structural Verilog: 9 circuits, main circuit main
module main (
);

  wire [31:0] adder_1_out, instruction_memory_1_instruction, NOP_mux_p3, PC_q;

  Register #(.width(32)) PC (.Q(PC_q));  // open: D, en, clk, clr
  Register #(.width(32)) Status ();  // open: D, en, Q, clk, clr
  Instruction_Memory instruction_memory_1 (.Read_Address(PC_q), .Instruction(instruction_memory_1_instruction));
  Adder #(.width(32)) adder_1 (.a(PC_q), .b(32'h1), .out(adder_1_out));  // open: cin, cout
  // mux NOP_mux: pin names not known; wires that end beside it: instruction_memory_1_instruction, {32{1'b0}}, NOP_mux_p3
  PipeRegister F_D (
    .PC_1(adder_1_out), .In1(NOP_mux_p3));  // open: enable, clear, Instruction, In2, PC_1_Out, Instruction_Out, Out1, Out2
  PipeRegister D_X ();  // open: enable, clear, PC_1, Instruction, In1, In2, PC_1_Out, Instruction_Out, Out1, Out2
  PipeRegister X_M ();  // open: enable, clear, PC_1, Instruction, In1, In2, PC_1_Out, Instruction_Out, Out1, Out2
  PipeRegister M_W ();  // open: enable, clear, PC_1, Instruction, In1, In2, PC_1_Out, Instruction_Out, Out1, Out2
endmodule

// Pipe Register
module PipeRegister (
  input  enable,
  input  clear,
  input  [31:0] PC_1,
  input  [31:0] Instruction,
  input  [31:0] In1,
  input  [31:0] In2,
  output [31:0] PC_1_Out,
  output [31:0] Instruction_Out,
  output [31:0] Out1,
  output [31:0] Out2
);

  wire clock_out;

  Clock clock (.out(clock_out));
  // AND_Gate and_1 has open pins: in0=enable, in1=clock_out, in2=clear, out=open

  assign Instruction_Out = Instruction;
  assign PC_1_Out = PC_1;
endmodule

// Insn Memory
module Instruction_Memory (
  input  [31:0] Read_Address,
  output [31:0] Instruction
);


  assign Instruction = Read_Address;
endmodule

module mux (
  input  [31:0] In0,
  input  [31:0] In1,
  input  select,
  output [31:0] Out
);
endmodule

module Execute (
);

  wire alu_1_out_4, alu_1_out_5, or_1_out, undriven, undriven_6, undriven_7, undriven_8, undriven_10,
       undriven_13, undriven_14, undriven_15, undriven_16, undriven_17, undriven_18, undriven_19,
       undriven_20, undriven_22, undriven_23, undriven_24;
  wire [31:0] alu_1_output, ALUOpBranch_out, ALUSrc_out, AMX_out, AWX_out, Chb_Module_out_2, Chb_out,
       Ctrl_setx_out, Cwc_Module_out_2, Cwc_out, Cyc_Module_out_2, Cyc_out, D_X_instruction_out, D_X_out1,
       D_X_out2, D_X_pc_1_out, Drop_2_out, Drop_Module_out_3, Drop_Module_out_4, Drop_out, multdiv_1_output,
       multdiv_1_status, MultDiv_2_out, Rdin_Module_out_2, Rdin_out, Stat_out, Status_q, undriven_2,
       undriven_3, undriven_4, undriven_5, undriven_9, undriven_11, undriven_12, undriven_21, undriven_25,
       undriven_26, undriven_27, undriven_28, X_M_instruction_out, X_M_out1, X_M_out2, X_M_pc_1_out;

  PipeRegister D_X (
    .enable(undriven_24), .clear(undriven), .PC_1(undriven_28), .Instruction(undriven_26), .In1(undriven_25),
    .In2(undriven_27), .PC_1_Out(D_X_pc_1_out), .Instruction_Out(D_X_instruction_out), .Out1(D_X_out1),
    .Out2(D_X_out2));
  Register #(.width(32)) Status (.D(Ctrl_setx_out), .Q(Status_q));  // open: en, clk, clr
  mux AWX (.In0(undriven_9), .In1(AMX_out), .Out(AWX_out), .select(undriven_10));
  mux AMX (.In0(undriven_5), .In1(D_X_out1), .Out(AMX_out), .select(undriven_7));
  mux ALUSrc (.In0(D_X_out2), .In1(undriven_4), .Out(ALUSrc_out), .select(undriven_6));
  mux Ctrl_setx (.In0(Stat_out), .In1(ALUSrc_out), .Out(Ctrl_setx_out), .select(undriven_8));
  mux ALUOpBranch (.In0(undriven_11), .In1(undriven_12), .Out(ALUOpBranch_out), .select(undriven_13));
  ALU alu_1 (
    .Input_A(AWX_out), .Input_B(ALUSrc_out), .out_4(alu_1_out_4), .out_5(alu_1_out_5), .Output(alu_1_output),
    .ALUOpIn(ALUOpBranch_out));
  MultDiv multdiv_1 (
    .Input_A(AWX_out), .Input_B(ALUSrc_out), .ctrl_mult(undriven_15), .ctrl_div(undriven_14),
    .Status(multdiv_1_status), .Output(multdiv_1_output));
  mux Stat (.In0(Status_q), .In1(multdiv_1_status), .Out(Stat_out), .select(or_1_out));
  mux MultDiv_2 (.In0(alu_1_output), .In1(multdiv_1_output), .Out(MultDiv_2_out), .select(or_1_out));
  or or_1 (or_1_out, undriven_14, undriven_15);
  mux Cyc (.In0(MultDiv_2_out), .In1(Cyc_Module_out_2), .Out(Cyc_out), .select(undriven_16));
  CycModule Cyc_Module (.in_1(undriven_2), .out_2(Cyc_Module_out_2));
  DropModule Drop_Module (.in_1(undriven_2), .in_2(undriven_3), .out_3(Drop_Module_out_3), .out_4(Drop_Module_out_4));
  mux Drop (.In0(Cyc_out), .In1(Drop_Module_out_3), .Out(Drop_out), .select(undriven_17));
  CycModule Cwc_Module (.in_1(undriven_2), .out_2(Cwc_Module_out_2));
  mux Chb (.In0(Cwc_out), .In1(Chb_Module_out_2), .Out(Chb_out), .select(undriven_19));
  mux Cwc (.In0(Drop_out), .In1(Cwc_Module_out_2), .Out(Cwc_out), .select(undriven_18));
  CycModule Chb_Module (.in_1(undriven_2), .out_2(Chb_Module_out_2));
  mux Rdin (.In0(Chb_out), .In1(Rdin_Module_out_2), .Out(Rdin_out), .select(undriven_20));
  CycModule Rdin_Module (.in_1(undriven_2), .out_2(Rdin_Module_out_2));
  mux Drop_2 (.In0(Drop_Module_out_4), .In1(D_X_instruction_out), .Out(Drop_2_out), .select(undriven_17));
  PipeRegister X_M (
    .enable(undriven_22), .clear(undriven_23), .PC_1(undriven_21), .Instruction(Drop_2_out), .In1(Rdin_out),
    .In2(ALUSrc_out), .PC_1_Out(X_M_pc_1_out), .Instruction_Out(X_M_instruction_out), .Out1(X_M_out1),
    .Out2(X_M_out2));

  // Notes on the sheet:
  //   R24
  //   R16 - R23
  //   Insn
  //   Ctrl_Mult
  //   Ctrl_Div
endmodule

module ALU (
  input  [31:0] Input_A,
  input  [31:0] Input_B,
  input  [31:0] ALUOpIn,
  output out_4,
  output out_5,
  output [31:0] Output
);
endmodule

// Mult/Div
module MultDiv (
  input  [31:0] Input_A,
  input  [31:0] Input_B,
  input  ctrl_mult,
  input  ctrl_div,
  output [31:0] Status,
  output [31:0] Output
);
endmodule

module CycModule (
  input  [31:0] in_1,
  output [31:0] out_2
);


  assign out_2 = in_1;
endmodule

module DropModule (
  input  [31:0] in_1,
  input  [31:0] in_2,
  output [31:0] out_3,
  output [31:0] out_4
);
endmodule
